// Logisim project cpu.circ as structural Verilog: 6 circuits, main circuit CPU
// 4
module CPU (
  output [47:0] cpu_out,
  output halt
);

  wire alu_1_carry, alu_1_negative, alu_1_overflow, alu_1_zero, ALU_instr, and_1_out, and_2_out, B_instr,
       clk, control_out, IR_we, LD_instr, PC_we, RA_we, RB_we, RD_we, reset, RF_we, RW_we, RZ_we, ST_instr;
  wire [2:0] multiplexer_2_out, multiplexer_3_out;
  wire [15:0] adder_1_out, alu_1_c, bit_extender_1_out, bit_extender_2_out, InsMem_data, multiplexer_1_out,
       multiplexer_4_out, multiplexer_5_out, RA_q, ram_1_dout, RB_q, RD_q, registerfile_1_a,
       registerfile_1_b, RW_q;

  Decoder #(.enable("false"), .select(2)) decoder_1 (
    .out0(ALU_instr), .out1(B_instr), .out2(LD_instr), .out3(ST_instr), .sel(cpu_out[31:30]));
  and and_1 (and_1_out, B_instr, RD_we, control_out);
  Multiplexer #(.width(16)) multiplexer_1 (
    .in0(16'h1), .in1(bit_extender_1_out), .out(multiplexer_1_out), .sel(and_1_out));
  assign bit_extender_1_out = {{13{cpu_out[25]}}, cpu_out[25:23]};  // Bit_Extender bit_extender_1
  Multiplexer #(.width(3)) multiplexer_2 (
    .in0(cpu_out[18:16]), .in1(cpu_out[25:23]), .out(multiplexer_2_out), .sel(ST_instr));
  Adder #(.width(16)) adder_1 (.a(cpu_out[47:32]), .b(multiplexer_1_out), .out(adder_1_out));  // open: cin, cout
  Register #(.width(16)) PC (.D(adder_1_out), .en(PC_we), .clk(clk), .Q(cpu_out[47:32]), .clr(reset));
  ROM #(.addrWidth(16), .dataWidth(16)) InsMem (.addr(cpu_out[47:32]), .data(InsMem_data));
  Clock u_clk (.out(clk));
  Button u_reset (.out(reset));
  FSM fsm_1 (
    .clk(clk), .reset(reset), .store(ST_instr), .branch(B_instr), .control(control_out), .IR_we(IR_we),
    .PC_we(PC_we), .RA_we(RA_we), .RB_we(RB_we), .RZ_we(RZ_we), .RD_we(RD_we), .RW_we(RW_we), .RF_we(RF_we));
  RegisterFile registerfile_1 (
    .Addr_A(cpu_out[22:20]), .Addr_B(multiplexer_2_out), .Addr_C(cpu_out[25:23]), .we(RF_we), .clk(clk),
    .reset(reset), .C(RW_q), .A(registerfile_1_a), .B(registerfile_1_b));
  Register #(.width(16)) RA (.D(registerfile_1_a), .en(RA_we), .clk(clk), .Q(RA_q), .clr(reset));
  Register #(.width(16)) RB (.D(registerfile_1_b), .en(RB_we), .clk(clk), .Q(RB_q), .clr(reset));
  Register #(.width(16)) IR (.D(InsMem_data), .en(IR_we), .clk(clk), .Q(cpu_out[31:16]), .clr(reset));
  Multiplexer #(.width(3)) multiplexer_3 (.in0(cpu_out[29:27]), .in1(3'b001), .out(multiplexer_3_out), .sel(B_instr));
  Multiplexer #(.width(16)) multiplexer_4 (
    .in0(RB_q), .in1(bit_extender_2_out), .out(multiplexer_4_out), .sel(cpu_out[26]));
  assign bit_extender_2_out = {{12{cpu_out[19]}}, cpu_out[19:16]};  // Bit_Extender bit_extender_2
  Comparator #(.width(16)) comparator_1 (.a(cpu_out[31:16]), .b(16'h4380), .eq(halt));  // open: gt, lt
  ALU alu_1 (
    .A(RA_q), .B(multiplexer_4_out), .fun(multiplexer_3_out), .carry(alu_1_carry), .C(alu_1_c),
    .overflow(alu_1_overflow), .negative(alu_1_negative), .zero(alu_1_zero));
  Register #(.width(16)) RD (.D(RB_q), .en(RD_we), .clk(clk), .Q(RD_q), .clr(reset));
  Register #(.width(16)) RZ (.D(alu_1_c), .en(RZ_we), .clk(clk), .Q(cpu_out[15:0]), .clr(reset));
  and and_2 (and_2_out, ST_instr, RW_we);
  Multiplexer #(.width(16)) multiplexer_5 (
    .in0(cpu_out[15:0]), .in1(ram_1_dout), .out(multiplexer_5_out), .sel(LD_instr));
  RAM #(.addrWidth(16), .dataWidth(16), .enables("line")) ram_1 (
    .addr(cpu_out[15:0]), .we(and_2_out), .clk(clk), .din(RD_q), .dout(ram_1_dout));
  BranchControl branchcontrol_1 (
    .condition(cpu_out[29:27]), .V(alu_1_overflow), .C(alu_1_carry), .Z(alu_1_zero), .N(alu_1_negative),
    .\bool (control_out));
  Register #(.width(16)) RW (.D(multiplexer_5_out), .en(RW_we), .clk(clk), .Q(RW_q), .clr(reset));

  // Other names for the same wires on the sheet: RZ_output[15:0] = cpu_out[15:0]; Addr_B[2:0] = cpu_out[18:16];
  //   IR_output[15:0] = cpu_out[31:16]; SrcOp2[3:0] = cpu_out[19:16]; SrcReg1[2:0] = cpu_out[22:20];
  //   DestReg[2:0] = cpu_out[25:23]; I = cpu_out[26]; AluOp[2:0] = cpu_out[29:27]; Opcode[1:0] = cpu_out[31:30];
  //   PC_output[15:0] = cpu_out[47:32]
endmodule

module ALU (
  input  [2:0] fun,
  input  [15:0] A,
  input  [15:0] B,
  output [15:0] C,
  output negative,
  output zero,
  output carry,
  output overflow
);

  wire adder_1_cout;
  wire [14:0] multiplexer_2_out, not_2_out;
  wire [15:0] adder_2_out, and_1_out, multiplexer_1_out, nor_1_out, not_1_out, or_1_out, shifter_1_out,
       shifter_2_out, shifter_3_out;

  assign not_1_out = ~B;  // NOT_Gate not_1, 16 bits wide
  assign not_2_out = ~B[14:0];  // NOT_Gate not_2, 15 bits wide
  Multiplexer #(.width(16)) multiplexer_1 (.in0(B), .in1(not_1_out), .out(multiplexer_1_out), .sel(fun[0]));
  Multiplexer #(.width(15)) multiplexer_2 (.in0(B[14:0]), .in1(not_2_out), .out(multiplexer_2_out), .sel(fun[0]));
  Adder #(.width(15)) adder_1 (.a(A[14:0]), .b(multiplexer_2_out), .cin(fun[0]), .cout(adder_1_cout));  // open: out
  Adder #(.width(16)) adder_2 (.a(A), .b(multiplexer_1_out), .out(adder_2_out), .cin(fun[0]), .cout(carry));
  assign and_1_out = A & B;  // AND_Gate and_1, 16 bits wide
  assign or_1_out = A | B;  // OR_Gate or_1, 16 bits wide
  assign nor_1_out = ~(A | B);  // NOR_Gate nor_1, 16 bits wide
  Shifter #(.width(16)) shifter_1 (.in(A), .\dist (B[3:0]), .out(shifter_1_out));
  Shifter #(.shift("lr"), .width(16)) shifter_2 (.in(A), .\dist (B[3:0]), .out(shifter_2_out));
  Shifter #(.shift("ar"), .width(16)) shifter_3 (.in(A), .\dist (B[3:0]), .out(shifter_3_out));
  Multiplexer #(.select(3), .width(16)) multiplexer_3 (
    .in0(adder_2_out), .in1(adder_2_out), .in2(and_1_out), .in3(or_1_out), .in4(nor_1_out),
    .in5(shifter_1_out), .in6(shifter_2_out), .in7(shifter_3_out), .out(C), .sel(fun));
  Comparator #(.width(16)) comparator_1 (.a(C), .b({16{1'b0}}), .eq(zero), .lt(negative));  // open: gt
  xor xor_1 (overflow, carry, adder_1_cout);
endmodule

module RegisterFile (
  input  [2:0] Addr_A,
  input  [2:0] Addr_B,
  input  [2:0] Addr_C,
  input  we,
  input  clk,
  input  reset,
  input  [15:0] C,
  output [15:0] A,
  output [15:0] B
);

  wire and_1_out, and_2_out, and_3_out, and_4_out, and_5_out, and_6_out, and_7_out, and_8_out,
       decoder_1_out0, decoder_1_out1, decoder_1_out2, decoder_1_out3, decoder_1_out4, decoder_1_out5,
       decoder_1_out6, decoder_1_out7;
  wire [15:0] R0_q, R1_q, R2_q, R3_q, R4_q, R5_q, R6_q, R7_q;

  Decoder #(.enable("false"), .select(3)) decoder_1 (
    .out0(decoder_1_out0), .out1(decoder_1_out1), .out2(decoder_1_out2), .out3(decoder_1_out3),
    .out4(decoder_1_out4), .out5(decoder_1_out5), .out6(decoder_1_out6), .out7(decoder_1_out7), .sel(Addr_C));
  and and_1 (and_1_out, decoder_1_out0, we);
  and and_2 (and_2_out, decoder_1_out1, we);
  and and_3 (and_3_out, decoder_1_out2, we);
  and and_4 (and_4_out, decoder_1_out3, we);
  Register #(.width(16)) R0 (.D(C), .en(and_1_out), .clk(clk), .Q(R0_q), .clr(reset));
  Register #(.width(16)) R1 (.D(C), .en(and_2_out), .clk(clk), .Q(R1_q), .clr(reset));
  Register #(.width(16)) R2 (.D(C), .en(and_3_out), .clk(clk), .Q(R2_q), .clr(reset));
  Register #(.width(16)) R3 (.D(C), .en(and_4_out), .clk(clk), .Q(R3_q), .clr(reset));
  Register #(.width(16)) R4 (.D(C), .en(and_5_out), .clk(clk), .Q(R4_q), .clr(reset));
  and and_5 (and_5_out, decoder_1_out4, we);
  Register #(.width(16)) R5 (.D(C), .en(and_6_out), .clk(clk), .Q(R5_q), .clr(reset));
  and and_6 (and_6_out, decoder_1_out5, we);
  Register #(.width(16)) R6 (.D(C), .en(and_7_out), .clk(clk), .Q(R6_q), .clr(reset));
  and and_7 (and_7_out, decoder_1_out6, we);
  Register #(.width(16)) R7 (.D(C), .en(and_8_out), .clk(clk), .Q(R7_q), .clr(reset));
  and and_8 (and_8_out, decoder_1_out7, we);
  Multiplexer #(.select(3), .width(16)) multiplexer_1 (
    .in0(R0_q), .in1(R1_q), .in2(R2_q), .in3(R3_q), .in4(R4_q), .in5(R5_q), .in6(R6_q), .in7(R7_q), .out(A),
    .sel(Addr_A));
  Multiplexer #(.select(3), .width(16)) multiplexer_2 (
    .in0(R0_q), .in1(R1_q), .in2(R2_q), .in3(R3_q), .in4(R4_q), .in5(R5_q), .in6(R6_q), .in7(R7_q), .out(B),
    .sel(Addr_B));
endmodule

module RegisterFileTester (
  output halt,
  output [15:0] A,
  output [15:0] B,
  output clk
);

  wire undriven;
  wire [2:0] Addr_A_data, Addr_B_data, Addr_C_data;
  wire [3:0] adder_1_out, addr_q;
  wire [15:0] C_data;

  Clock clock_1 (.out(clk));
  ROM #(.addrWidth(4), .dataWidth(3)) Addr_A (.addr(addr_q), .data(Addr_A_data));
  ROM #(.addrWidth(4), .dataWidth(3)) Addr_B (.addr(addr_q), .data(Addr_B_data));
  ROM #(.addrWidth(4), .dataWidth(3)) Addr_C (.addr(addr_q), .data(Addr_C_data));
  ROM #(.addrWidth(4), .dataWidth(1)) we (.addr(addr_q));  // open: data
  ROM #(.addrWidth(4), .dataWidth(16)) C (.addr(addr_q), .data(C_data));
  Adder #(.width(4)) adder_1 (.a(addr_q), .b(4'b0001), .out(adder_1_out), .cin(1'b0));  // open: cout
  Register #(.width(4)) addr (.D(adder_1_out), .en(1'b1), .clk(clk), .Q(addr_q), .clr(1'b0));
  Comparator #(.width(4)) comparator_1 (.a(addr_q), .b(4'b1111), .eq(halt));  // open: gt, lt
  RegisterFile registerfile_1 (
    .Addr_A(Addr_A_data), .Addr_B(Addr_B_data), .Addr_C(Addr_C_data), .we(undriven), .clk(clk), .reset(1'b0),
    .C(C_data), .A(A), .B(B));

  // Notes on the sheet:
  //   contents of Addr_A (hex, n*v repeats v):
  //   5 2 7 3 2 0 2 6 2 4 1 3 5 5 2 6
  //   contents of Addr_B (hex, n*v repeats v):
  //   4 4 6 0 2 3 5 5 5 0 0 4 5 3 7 5
  //   contents of Addr_C (hex, n*v repeats v):
  //   0 5 0 5 5 7 2 3 6 4 0 4 7 7 4 6
  //   contents of we (hex, n*v repeats v):
  //   0 0 0 1 0 0 1 0 0 0 1 1 0 0 1 1
  //   contents of C (hex, n*v repeats v):
  //   1 4 c f 0 5 9 7 c b 9 f b 9 1 e
endmodule

module FSM (
  input  clk,
  input  reset,
  input  store,
  input  branch,
  input  control,
  output IR_we,
  output PC_we,
  output RA_we,
  output RB_we,
  output RZ_we,
  output RD_we,
  output RW_we,
  output RF_we
);

  wire and_1_out, and_2_out, comparator_1_eq, comparator_2_eq, demultiplexer_1_out4, or_1_out, or_2_out;
  wire [2:0] adder_1_out, register_1_q;

  Register #(.width(3)) register_1 (.D(adder_1_out), .clk(clk), .Q(register_1_q), .clr(or_1_out));  // open: en
  Adder #(.width(3)) adder_1 (.a(register_1_q), .b(3'b001), .out(adder_1_out));  // open: cin, cout
  or or_1 (or_1_out, reset, and_1_out, comparator_2_eq);
  and and_1 (and_1_out, control, branch, comparator_1_eq);
  Comparator #(.width(3)) comparator_1 (.a(register_1_q), .b(3'b011), .eq(comparator_1_eq));  // open: gt, lt
  Comparator #(.width(3)) comparator_2 (.a(register_1_q), .b(3'b101), .eq(comparator_2_eq));  // open: gt, lt
  Demultiplexer #(.select(3)) demultiplexer_1 (
    .out0(IR_we), .out1(RA_we), .out2(RD_we), .out3(RW_we), .out4(demultiplexer_1_out4), .in(1'b1),
    .sel(register_1_q));  // open: out5, out6, out7
  or or_2 (or_2_out, store, branch);
  Multiplexer multiplexer_1 (.in0(demultiplexer_1_out4), .in1(1'b0), .out(RF_we), .sel(or_2_out));
  and and_2 (and_2_out, RD_we, branch, control);
  or or_3 (PC_we, IR_we, and_2_out);

  assign RB_we = RA_we;
  assign RZ_we = RD_we;
endmodule

module BranchControl (
  input  [2:0] condition,
  input  V,
  input  C,
  input  Z,
  input  N,
  output \bool 
);

  wire and_1_out, and_2_out, and_3_out, and_4_out, and_5_out, and_6_out, and_7_out, decoder_1_out0,
       decoder_1_out1, decoder_1_out2, decoder_1_out3, decoder_1_out4, decoder_1_out5, or_1_out, xnor_1_out,
       xor_1_out;

  Decoder #(.enable("false"), .select(3)) decoder_1 (
    .out0(decoder_1_out0), .out1(decoder_1_out1), .out2(decoder_1_out2), .out3(decoder_1_out3),
    .out4(decoder_1_out4), .out5(decoder_1_out5), .sel(condition));  // open: out6, out7
  xor xor_1 (xor_1_out, V, N);
  xnor xnor_1 (xnor_1_out, V, N);
  or or_1 (or_1_out, xor_1_out, Z);
  and and_1 (and_1_out, xnor_1_out, ~Z);  // AND_Gate
  and and_2 (and_2_out, decoder_1_out0, Z);
  and and_3 (and_3_out, decoder_1_out1, ~Z);  // AND_Gate
  and and_4 (and_4_out, decoder_1_out2, xor_1_out);
  and and_5 (and_5_out, decoder_1_out3, or_1_out);
  and and_6 (and_6_out, decoder_1_out4, and_1_out);
  and and_7 (and_7_out, decoder_1_out5, xnor_1_out);
  or or_2 (\bool , and_2_out, and_3_out, and_4_out, and_5_out, and_6_out, and_7_out);
endmodule
